# Fritzing sketch sketch (saved by Fritzing 0.9.3b)
breadboards: 1

parts:
  U1 = ESP8266 WiFi Module [part_number=ESP8266]
  IC1 = A4950 [package=soicn]
  U2 = Voltage Regulator - 3.3V [package="TO220 [THT]"]
  J1 = Power Jack [package=power_jack_slot]
  C1 = Electrolytic Capacitor [capacitance=22µF package="0807 [SMD, electrolytic]"]
  C2 = Electrolytic Capacitor [capacitance=22µF package="0807 [SMD, electrolytic]"]
  L1 = Solenoid
  U3 = SWITCH_SPDT [package=kps-1290]
  S2 = Pushbutton [package="[THT]"]
  S3 = Pushbutton [package="[THT]"]
  S4 = Pushbutton [package="[THT]"]
  C3 = Capacitor [package=cap-pth-small2]

nets:
  N1: U1.VCC, U1.GPIO_2, U1.CH_PD, U1.GPIO_12, U1.GPIO_13, IC1.IN2, IC1.IN1, IC1.VREF, U2.output_voltage, C1.+, S3.Pin_1, S3.Pin_2, S3.Pin_3, S3.Pin_4, S4.Pin_1, S4.Pin_2, S4.Pin_3, S4.Pin_4
  N2: U1.GPIO_0, U3.P
  GND: U1.GND, U1.GPIO_15, U1.GPIO_16, U1.REST, IC1.GND, IC1.LSS, U2.GND, J1.GND, C1.-, C2.-, U3.S, S2.Pin_1, S2.Pin_2, C3.1
  N3: IC1.VBB, U2.input_voltage, J1.PWR, C2.+, C3.2
  N4: IC1.OUT1, L1.pin2
  N5: IC1.OUT2, L1.pin1
